# Fritzing sketch Diagnostic_System_Sketch_1.0 (saved by Fritzing 0.9.3b)

parts:
  Arduino_Uno1 = Arduino Uno (Rev3)
  Part7 = Bluetooth HC-05 Macho
  Part6 = KY-023 Dual Axis Joystick Module [package="Breakout board"]

nets:
  N1: Arduino_Uno1.A0, Part6.VRx
  N2: Arduino_Uno1.A1, Part6.VRy
  N3: Arduino_Uno1.D0/RX, Part7.TXD
  N4: Arduino_Uno1.D1/TX, Part7.RXD
  5V: Arduino_Uno1.5V, Part7.VCC, Part6.+5V
  GND: Arduino_Uno1.GND, Part7.GND, Part6.GND

notes:
  Bluetooth מודול
  ג'ויסטיק
