# Fritzing sketch Helping_System_Sketch (saved by Fritzing 0.9.3b)
breadboards: 1

parts:
  Q1 = NPN-Transistor [package="TO92 [THT]"]
  LED1 = Infrared LED - 5mm [package="5 mm [THT]"]
  IR_Receiver1 = IR_Receiver
  Arduino_Uno = Arduino Uno (Rev3)
  Part2 = LCD1602-I2C
  S1 = Round Pushbutton
  S2 = Round Pushbutton
  Part3 = KY-023 Dual Axis Joystick Module [package="Breakout board"]
  Part4 = Bluetooth HC-05 Macho
  R1 = Resistor [tolerance=±5% resistance=220 package=THT]
  buz1 = Piezo Buzzer
  R2 = Resistor [tolerance=±5% resistance=220 package=THT]
  KY-1 = Keyes Relay [package=THT]
  JACK1 = 2.1mm Barrel Jack with Terminal Block
  Bulb_220v1 = LEDs [package=led10mm]
  Bulb_220v2 = LEDs [package=led10mm]  # not connected

nets:
  GND: Q1.E, IR_Receiver1.GND, Arduino_Uno.D9_PWM, Arduino_Uno.D12/MISO, Arduino_Uno.GND, Part2.GND, Part3.GND, Part4.GND, R1.Pin_0, buz1.pin_2, R2.Pin_0, KY-1.ground
  N1: Q1.B, Arduino_Uno.D3_PWM
  N2: Q1.C, LED1.cathode
  VCC: LED1.anode, IR_Receiver1.VCC, Arduino_Uno.5V, Part2.VCC, S1.leg0, S2.leg0, Part3.+5V, Part4.VCC, KY-1.power
  N3: IR_Receiver1.OUT, Arduino_Uno.D11_PWM/MOSI
  N4: Arduino_Uno.A0, Part3.VRx
  N5: Arduino_Uno.A1, Part3.VRy
  N6: Arduino_Uno.A4/SDA, Part2.SCL
  N7: Arduino_Uno.A5/SCL, Part2.SDA
  N8: Arduino_Uno.D8, KY-1.signal
  N9: Arduino_Uno.D0/RX, Part4.TXD
  N10: Arduino_Uno.D1/TX, Part4.RXD
  N11: Arduino_Uno.D7, buz1.pin_1
  N12: S1.leg1, R1.Pin_1
  N13: S2.leg1, R2.Pin_1
  N14: KY-1.C, Bulb_220v1.Line
  N15: KY-1.NO, JACK1.POS
  N16: JACK1.NEG, Bulb_220v1.Neutral

custom parts:
  Infrared LED - 5mm: A generic infrared LED (~1.2V)
  IR_Receiver: 赤外線受信モジュール GP1UXC41QS
  LCD1602-I2C: A standard character display, usually with 2x16 characters. Comes in many colors with LCM1602 IIC attached.
  Piezo Buzzer: Part from https://www.nutsvolts.com/magazine/article/november2012_SmileysWorkshop modified to be .3 in spacing to match the adafruit buzzer 5V breadboard friendly part.
  Keyes Relay: The Keyes 5V relay module is suitable for SCM development, home appliance control. It uses a 5V~12V TIL control signal which can control DC / AC signal.
  LEDs: Bulb
  LEDs: Bulb
