# Fritzing sketch Helping_System_Sketch_2.0 (saved by Fritzing 0.9.3b)
breadboards: 1

parts:
  Arduino_Uno1 = Arduino Uno (Rev3)
  Q2 = NPN-Transistor [package="TO92 [THT]"]
  Part7 = Bluetooth HC-05 Macho
  R3 = Resistor [tolerance=±5% resistance=220 package=THT]
  R4 = Resistor [tolerance=±5% resistance=220 package=THT]
  KY-2 = Keyes Relay [package=THT]
  Part6 = KY-023 Dual Axis Joystick Module [package="Breakout board"]
  JACK2 = 2.1mm Barrel Jack with Terminal Block
  buz2 = Piezo Buzzer
  S3 = Round Pushbutton
  IR_Receiver2 = IR_Receiver
  Part5 = LCD1602-I2C
  LED2 = Infrared LED - 5mm [package="5 mm [THT]"]
  S4 = Round Pushbutton
  Bulb_220v2 = LEDs [package=led10mm]

nets:
  N1: Arduino_Uno1.A0, Part6.VRx
  N2: Arduino_Uno1.A1, Part6.VRy
  N3: Arduino_Uno1.A4/SDA, Part5.SCL
  N4: Arduino_Uno1.A5/SCL, Part5.SDA
  N5: Arduino_Uno1.D8, KY-2.signal
  GND: Arduino_Uno1.D9_PWM, Arduino_Uno1.D12/MISO, Arduino_Uno1.GND, Q2.E, Part7.GND, R3.Pin_0, R4.Pin_0, KY-2.ground, Part6.GND, buz2.pin_2, IR_Receiver2.GND, Part5.GND
  N6: Arduino_Uno1.D11_PWM/MOSI, IR_Receiver2.OUT
  N7: Arduino_Uno1.D0/RX, Part7.TXD
  N8: Arduino_Uno1.D1/TX, Part7.RXD
  N9: Arduino_Uno1.D3_PWM, Q2.B
  N10: Arduino_Uno1.D7, buz2.pin_1
  VCC: Arduino_Uno1.5V, Part7.VCC, KY-2.power, Part6.+5V, S3.leg0, IR_Receiver2.VCC, Part5.VCC, LED2.anode, S4.leg0
  N11: Q2.C, LED2.cathode
  N12: R3.Pin_1, S4.leg1
  N13: R4.Pin_1, S3.leg1
  N14: KY-2.C, Bulb_220v2.Line
  N15: KY-2.NO, JACK2.POS
  N16: JACK2.NEG, Bulb_220v2.Neutral

notes:
  Bluetooth מודול
  טרנזיסטור
  2N2222
  Resistors 220 Ohm
  ממסר Relay
  חשמל במתח 220 וולט (AC)
  זמזם
  כפתורי תכנות
  לד שידור IR
  מסך LCD
  ג'ויסטיק
  חיישן קליטת IR

custom parts:
  Keyes Relay: The Keyes 5V relay module is suitable for SCM development, home appliance control. It uses a 5V~12V TIL control signal which can control DC / AC signal.
  Piezo Buzzer: Part from https://www.nutsvolts.com/magazine/article/november2012_SmileysWorkshop modified to be .3 in spacing to match the adafruit buzzer 5V breadboard friendly part.
  IR_Receiver: 赤外線受信モジュール GP1UXC41QS
  LCD1602-I2C: A standard character display, usually with 2x16 characters. Comes in many colors with LCM1602 IIC attached.
  Infrared LED - 5mm: A generic infrared LED (~1.2V)
  LEDs: Bulb
