# Fritzing sketch IR_Reciever_Transmitter_Sketch_1.0 (saved by Fritzing 0.9.3b)
breadboards: 1

parts:
  Arduino_Uno1 = Arduino Uno (Rev3)
  Q2 = NPN-Transistor [package="TO92 [THT]"]
  IR_Receiver2 = IR_Receiver
  LED2 = Infrared LED - 5mm [package="5 mm [THT]"]

nets:
  N1: Arduino_Uno1.D11_PWM/MOSI, IR_Receiver2.OUT
  N2: Arduino_Uno1.D3_PWM, Q2.B
  5V: Arduino_Uno1.5V, IR_Receiver2.VCC, LED2.anode
  GND: Arduino_Uno1.GND, Q2.E, IR_Receiver2.GND
  N3: Q2.C, LED2.cathode

notes:
  טרנזיסטור
  2N2222
  לד שידור IR
  חיישן קליטת IR

custom parts:
  IR_Receiver: 赤外線受信モジュール GP1UXC41QS
  Infrared LED - 5mm: A generic infrared LED (~1.2V)
